# Fritzing sketch arduino_light (saved by Fritzing 0.9.3b)
circuit board: 5.95923cm x 6.3306cm
breadboards: 1

parts:
  Arduino_UNO = Arduino Uno (Rev3)
  Relay_5V = Keyes Relay [package=THT]
  Part1 = LCD1602-I2C
  S1 = Momentary Switch [package=ksa_sealed_tac_switch]
  S2 = Momentary Switch [package=ksa_sealed_tac_switch]
  S3 = Momentary Switch [package=ksa_sealed_tac_switch]

nets (from the breadboard view):
  N1: Arduino_UNO.A4/SDA, Part1.SDA
  N2: Arduino_UNO.A5/SCL, Part1.SCL
  N3: Arduino_UNO.D8, Relay_5V.signal
  GND: Arduino_UNO.GND, Relay_5V.ground, Part1.GND, S1.1, S2.1, S3.1
  N4: Arduino_UNO.D1/TX, S3.4
  N5: Arduino_UNO.D2, S2.4
  N6: Arduino_UNO.D3_PWM, S1.4
  5V: Arduino_UNO.5V, Relay_5V.power, Part1.VCC

custom parts:
  Keyes Relay: The Keyes 5V relay module is suitable for SCM development, home appliance control. It uses a 5V~12V TIL control signal which can control DC / AC signal.
  LCD1602-I2C: A standard character display, usually with 2x16 characters. Comes in many colors with LCM1602 IIC attached.

// code stored in the sketch: bluetoothLight.ino
char blueToothVal;           //value sent over via bluetooth
char lastValue;              //stores last state of device (on/off)
 
void setup()
{
 Serial.begin(9600); 
 pinMode(13,OUTPUT);
 pinMode(12,INPUT);
}
 
 
void loop()
{
  if(Serial.available())
  {//if there is data being recieved
    blueToothVal=Serial.read(); //read it
  }
  if (blueToothVal=='n')
  {//if value from bluetooth serial is n
    digitalWrite(13,HIGH);            //switch on LED
    if (lastValue!='n')
      Serial.println(F("LED is on")); //print LED is on
    lastValue=blueToothVal;
  }
  else if (blueToothVal=='f')
  {//if value from bluetooth serial is n
    digitalWrite(13,LOW);             //turn off LED
    if (lastValue!='f')
      Serial.println(F("LED is off")); //print LED is on
    lastValue=blueToothVal;
  }
  delay(250);
}
